// Logisim project circ.circ as structural Verilog: 7 circuits, main circuit counter10
module counter10 (
  input  b3,
  input  b2,
  input  b1,
  input  b0,
  output b3_6459a22e,
  output b2_1cbd16a1,
  output b1_bd1f244d,
  output b0_0b286615,
  output carry
);

  wire and_2_out, and_3_out, and_4_out, and_5_out, and_6_out, and_7_out, and_8_out, not_1_out, not_2_out,
       not_3_out, not_4_out, not_5_out, not_6_out, not_7_out;

  not not_1 (not_1_out, b0);
  not not_2 (not_2_out, b2);
  not not_3 (not_3_out, b1);
  not not_4 (not_4_out, b0);
  not not_5 (not_5_out, b3);
  not not_6 (not_6_out, b1);
  not not_7 (not_7_out, b0);
  not not_8 (b0_0b286615, b0);
  and and_1 (carry, b3, b0);
  and and_2 (and_2_out, b2, b1, b0);
  and and_3 (and_3_out, b3, not_1_out);
  and and_4 (and_4_out, not_2_out, b1, b0);
  and and_5 (and_5_out, b2, not_3_out);
  and and_6 (and_6_out, b2, not_4_out);
  and and_7 (and_7_out, not_5_out, not_6_out, b0);
  and and_8 (and_8_out, b1, not_7_out);
  or or_1 (b3_6459a22e, and_2_out, and_3_out);
  or or_2 (b2_1cbd16a1, and_4_out, and_5_out, and_6_out);
  or or_3 (b1_bd1f244d, and_7_out, and_8_out);
endmodule

module main (
);

  wire clock_1_out;

  Clock clock_1 (.out(clock_1_out));
  clock24h_display clock24h_display_1 (.clk_10ths(clock_1_out));  // open: a0, b0, c0, d0, e0, f0, g0, a1, b1, c1, d1, e1, f1, g1, a2, b2, c2, d2, e2, f2, g2, a3, b3, c3, d3, e3, f3, g3, a4, b4, c4, d4, e4, f4, g4, a5, b5, c5, d5, e5, f5, g5, a6, b6, c6, d6, e6, f6, g6, a7, b7, c7, d7, e7, f7, g7
  _7_Segment_Display L_7_Segment_Display_1 ();  // open: g, f, a, b, e, d, c, dp
  _7_Segment_Display L_7_Segment_Display_3 ();  // open: g, f, a, b, e, d, c, dp
  _7_Segment_Display L_7_Segment_Display_2 ();  // open: g, f, a, b, e, d, c, dp
  _7_Segment_Display L_7_Segment_Display_4 ();  // open: g, f, a, b, e, d, c, dp
  _7_Segment_Display L_7_Segment_Display_5 ();  // open: g, f, a, b, e, d, c, dp
  _7_Segment_Display L_7_Segment_Display_6 ();  // open: g, f, a, b, e, d, c, dp
endmodule

module bin2display (
  input  b0,
  input  b1,
  input  b2,
  input  b3,
  output a,
  output b,
  output c,
  output d,
  output e,
  output f,
  output g
);

  wire and_1_out, and_2_out, and_3_out, and_4_out, and_5_out, and_6_out, and_7_out, and_8_out, and_9_out,
       and_10_out, and_11_out, and_12_out, and_13_out, and_14_out, and_15_out, and_16_out, and_17_out,
       and_18_out, and_19_out, and_20_out, and_21_out, and_22_out, and_23_out, and_24_out, and_25_out,
       and_26_out, and_27_out, and_28_out, and_29_out, and_30_out, and_31_out, and_32_out, and_33_out,
       and_34_out, and_35_out, not_1_out, not_2_out, not_3_out, not_4_out, not_5_out, not_6_out, not_7_out,
       not_8_out, not_9_out, not_10_out, not_11_out, not_12_out, not_13_out, not_14_out, not_15_out,
       not_16_out, not_17_out, not_18_out, not_19_out, not_20_out, not_21_out, not_22_out, not_23_out,
       not_24_out, not_25_out, not_26_out, not_27_out, not_28_out, not_29_out, not_30_out, not_31_out,
       not_32_out, not_33_out, not_34_out, not_35_out, not_36_out, not_37_out, not_38_out, not_39_out,
       not_40_out, not_41_out, not_42_out, not_43_out;

  not not_1 (not_1_out, b2);
  not not_2 (not_2_out, b0);
  not not_3 (not_3_out, b3);
  not not_4 (not_4_out, b3);
  not not_5 (not_5_out, b2);
  not not_6 (not_6_out, b1);
  not not_7 (not_7_out, b0);
  not not_8 (not_8_out, b0);
  not not_9 (not_9_out, b1);
  not not_10 (not_10_out, b3);
  not not_11 (not_11_out, b0);
  not not_12 (not_12_out, b2);
  not not_13 (not_13_out, b1);
  not not_14 (not_14_out, b2);
  not not_15 (not_15_out, b1);
  not not_16 (not_16_out, b3);
  not not_17 (not_17_out, b1);
  not not_18 (not_18_out, b2);
  not not_19 (not_19_out, b2);
  not not_20 (not_20_out, b3);
  not not_21 (not_21_out, b1);
  not not_22 (not_22_out, b2);
  not not_23 (not_23_out, b0);
  not not_24 (not_24_out, b2);
  not not_25 (not_25_out, b3);
  not not_26 (not_26_out, b1);
  not not_27 (not_27_out, b0);
  not not_28 (not_28_out, b1);
  not not_29 (not_29_out, b2);
  not not_30 (not_30_out, b0);
  not not_31 (not_31_out, b2);
  not not_32 (not_32_out, b0);
  not not_33 (not_33_out, b0);
  not not_34 (not_34_out, b1);
  not not_35 (not_35_out, b2);
  not not_36 (not_36_out, b0);
  not not_37 (not_37_out, b1);
  not not_38 (not_38_out, b3);
  not not_39 (not_39_out, b2);
  not not_40 (not_40_out, b1);
  not not_41 (not_41_out, b3);
  not not_42 (not_42_out, b0);
  not not_43 (not_43_out, b2);
  and and_1 (and_1_out, not_1_out, not_2_out);
  and and_2 (and_2_out, not_3_out, b1);
  and and_3 (and_3_out, not_4_out, b2, b0);
  and and_4 (and_4_out, b2, b1);
  and and_5 (and_5_out, b3, not_5_out, not_6_out);
  and and_6 (and_6_out, b3, not_7_out);
  and and_7 (and_7_out, not_8_out, not_9_out, not_10_out);
  and and_8 (and_8_out, not_11_out, not_12_out);
  and and_9 (and_9_out, not_13_out, not_14_out);
  and and_10 (and_10_out, b0, not_15_out, b3);
  and and_11 (and_11_out, b0, b1, not_16_out);
  and and_12 (and_12_out, not_17_out, not_18_out);
  and and_13 (and_13_out, not_19_out, b3);
  and and_14 (and_14_out, b2, not_20_out);
  and and_15 (and_15_out, b0, not_21_out);
  and and_16 (and_16_out, b0, not_22_out);
  and and_17 (and_17_out, not_23_out, not_24_out, not_25_out);
  and and_18 (and_18_out, not_26_out, b3);
  and and_19 (and_19_out, not_27_out, b1, b2);
  and and_20 (and_20_out, b0, not_28_out, b2);
  and and_21 (and_21_out, b0, b1, not_29_out);
  and and_22 (and_22_out, not_30_out, not_31_out);
  and and_23 (and_23_out, b2, b3);
  and and_24 (and_24_out, not_32_out, b1);
  and and_25 (and_25_out, b1, b3);
  and and_26 (and_26_out, not_33_out, not_34_out);
  and and_27 (and_27_out, not_35_out, b3);
  and and_28 (and_28_out, not_36_out, b2);
  and and_29 (and_29_out, not_37_out, b2, not_38_out);
  and and_30 (and_30_out, b1, b3);
  and and_31 (and_31_out, not_39_out, b3);
  and and_32 (and_32_out, not_40_out, b2, not_41_out);
  and and_33 (and_33_out, not_42_out, b1);
  and and_34 (and_34_out, b1, not_43_out);
  and and_35 (and_35_out, b0, b3);
  or or_1 (a, and_1_out, and_2_out, and_3_out, and_4_out, and_5_out, and_6_out);
  or or_2 (b, and_7_out, and_8_out, and_9_out, and_10_out, and_11_out);
  or or_3 (c, and_12_out, and_13_out, and_14_out, and_15_out, and_16_out);
  or or_4 (d, and_17_out, and_18_out, and_19_out, and_20_out, and_21_out);
  or or_5 (e, and_22_out, and_23_out, and_24_out, and_25_out);
  or or_6 (f, and_26_out, and_27_out, and_28_out, and_29_out, and_30_out);
  or or_7 (g, and_31_out, and_32_out, and_33_out, and_34_out, and_35_out);
endmodule

module L_2bit_counter_3d0c5adb (
  input  B1,
  input  B0,
  output E1,
  output E0,
  output N
);

  wire not_1_out, not_2_out;

  not not_1 (not_1_out, B1);
  and and_1 (E0, not_1_out, not_2_out);
  not not_2 (not_2_out, B0);

  assign E1 = B0;
  assign N = B1;
endmodule

module L_6bit_counter_ba3864c1 (
  input  B2,
  input  B1,
  input  B0,
  output E2,
  output E1,
  output E0,
  output N
);

  wire and_2_out, and_3_out, and_4_out, and_5_out, and_6_out, and_7_out, not_1_out, not_2_out, not_3_out,
       not_4_out, not_5_out, not_6_out, not_7_out, not_8_out;

  not not_1 (not_1_out, B1);
  not not_2 (not_2_out, B1);
  not not_3 (not_3_out, B2);
  not not_4 (not_4_out, B0);
  not not_5 (not_5_out, B2);
  not not_6 (not_6_out, B0);
  not not_7 (not_7_out, B1);
  not not_8 (not_8_out, B0);
  and and_1 (N, B2, B1);
  and and_2 (and_2_out, B1, B0);
  and and_3 (and_3_out, B2, not_1_out);
  and and_4 (and_4_out, not_2_out, B0);
  and and_5 (and_5_out, not_3_out, B1, not_4_out);
  and and_6 (and_6_out, not_5_out, not_6_out);
  and and_7 (and_7_out, not_7_out, not_8_out);
  or or_1 (E2, and_2_out, and_3_out);
  or or_2 (E1, and_4_out, and_5_out);
  or or_3 (E0, and_6_out, and_7_out);
endmodule

module clock24h (
  input  clock_10thsecond,
  output b00,
  output b01,
  output b02,
  output b03,
  output b10,
  output b11,
  output b12,
  output b13,
  output b20,
  output b21,
  output b22,
  output b23,
  output b30,
  output b31,
  output b32,
  output b40,
  output b41,
  output b42,
  output b43,
  output b50,
  output b51,
  output b52,
  output b60,
  output b61,
  output b62,
  output b63,
  output b71,
  output b72
);

  wire counter10_1_b0_0b286615, counter10_1_b1_bd1f244d, counter10_1_b2_1cbd16a1, counter10_1_b3_6459a22e,
       counter10_1_carry, counter10_2_b0_0b286615, counter10_2_b1_bd1f244d, counter10_2_b2_1cbd16a1,
       counter10_2_b3_6459a22e, counter10_2_carry, counter10_3_b0_0b286615, counter10_3_b1_bd1f244d,
       counter10_3_b2_1cbd16a1, counter10_3_b3_6459a22e, counter10_3_carry, counter10_4_b0_0b286615,
       counter10_4_b1_bd1f244d, counter10_4_b2_1cbd16a1, counter10_4_b3_6459a22e, counter10_4_carry,
       counter10_5_b0_0b286615, counter10_5_b1_bd1f244d, counter10_5_b2_1cbd16a1, counter10_5_b3_6459a22e,
       counter10_5_carry, L_2bit_counter_3d0c5adb_1_e0, L_2bit_counter_3d0c5adb_1_e1,
       L_6bit_counter_ba3864c1_1_e0, L_6bit_counter_ba3864c1_1_e1, L_6bit_counter_ba3864c1_1_e2,
       L_6bit_counter_ba3864c1_1_n, L_6bit_counter_ba3864c1_2_e0, L_6bit_counter_ba3864c1_2_e1,
       L_6bit_counter_ba3864c1_2_e2, L_6bit_counter_ba3864c1_2_n;

  counter10 counter10_1 (
    .b3(b03), .b2(b02), .b1(b01), .b0(b00), .b3_6459a22e(counter10_1_b3_6459a22e),
    .b2_1cbd16a1(counter10_1_b2_1cbd16a1), .b1_bd1f244d(counter10_1_b1_bd1f244d),
    .b0_0b286615(counter10_1_b0_0b286615), .carry(counter10_1_carry));
  D_Flip_Flop d_ff_1 (.D(counter10_1_b3_6459a22e), .clk(clock_10thsecond), .Q(b03));  // open: Qn, preset, reset
  D_Flip_Flop d_ff_2 (.D(counter10_1_b2_1cbd16a1), .clk(clock_10thsecond), .Q(b02));  // open: Qn, preset, reset
  D_Flip_Flop d_ff_3 (.D(counter10_1_b1_bd1f244d), .clk(clock_10thsecond), .Q(b01));  // open: Qn, preset, reset
  D_Flip_Flop d_ff_4 (.D(counter10_1_b0_0b286615), .clk(clock_10thsecond), .Q(b00));  // open: Qn, preset, reset
  counter10 counter10_2 (
    .b3(b13), .b2(b12), .b1(b11), .b0(b10), .b3_6459a22e(counter10_2_b3_6459a22e),
    .b2_1cbd16a1(counter10_2_b2_1cbd16a1), .b1_bd1f244d(counter10_2_b1_bd1f244d),
    .b0_0b286615(counter10_2_b0_0b286615), .carry(counter10_2_carry));
  D_Flip_Flop d_ff_5 (.D(counter10_2_b3_6459a22e), .clk(counter10_1_carry), .Q(b13));  // open: Qn, preset, reset
  D_Flip_Flop d_ff_6 (.D(counter10_2_b2_1cbd16a1), .clk(counter10_1_carry), .Q(b12));  // open: Qn, preset, reset
  D_Flip_Flop d_ff_7 (.D(counter10_2_b1_bd1f244d), .clk(counter10_1_carry), .Q(b11));  // open: Qn, preset, reset
  D_Flip_Flop d_ff_8 (.D(counter10_2_b0_0b286615), .clk(counter10_1_carry), .Q(b10));  // open: Qn, preset, reset
  counter10 counter10_3 (
    .b3(b23), .b2(b22), .b1(b21), .b0(b20), .b3_6459a22e(counter10_3_b3_6459a22e),
    .b2_1cbd16a1(counter10_3_b2_1cbd16a1), .b1_bd1f244d(counter10_3_b1_bd1f244d),
    .b0_0b286615(counter10_3_b0_0b286615), .carry(counter10_3_carry));
  D_Flip_Flop d_ff_9 (.D(counter10_3_b3_6459a22e), .clk(counter10_2_carry), .Q(b23));  // open: Qn, preset, reset
  D_Flip_Flop d_ff_10 (.D(counter10_3_b2_1cbd16a1), .clk(counter10_2_carry), .Q(b22));  // open: Qn, preset, reset
  D_Flip_Flop d_ff_11 (.D(counter10_3_b1_bd1f244d), .clk(counter10_2_carry), .Q(b21));  // open: Qn, preset, reset
  D_Flip_Flop d_ff_12 (.D(counter10_3_b0_0b286615), .clk(counter10_2_carry), .Q(b20));  // open: Qn, preset, reset
  L_6bit_counter_ba3864c1 L_6bit_counter_ba3864c1_1 (
    .B2(b32), .B1(b31), .B0(b30), .E2(L_6bit_counter_ba3864c1_1_e2), .E1(L_6bit_counter_ba3864c1_1_e1),
    .E0(L_6bit_counter_ba3864c1_1_e0), .N(L_6bit_counter_ba3864c1_1_n));
  D_Flip_Flop d_ff_13 (.D(L_6bit_counter_ba3864c1_1_e2), .clk(counter10_3_carry), .Q(b32));  // open: Qn, preset, reset
  D_Flip_Flop d_ff_14 (.D(L_6bit_counter_ba3864c1_1_e1), .clk(counter10_3_carry), .Q(b31));  // open: Qn, preset, reset
  D_Flip_Flop d_ff_15 (.D(L_6bit_counter_ba3864c1_1_e0), .clk(counter10_3_carry), .Q(b30));  // open: Qn, preset, reset
  counter10 counter10_4 (
    .b3(b43), .b2(b42), .b1(b41), .b0(b40), .b3_6459a22e(counter10_4_b3_6459a22e),
    .b2_1cbd16a1(counter10_4_b2_1cbd16a1), .b1_bd1f244d(counter10_4_b1_bd1f244d),
    .b0_0b286615(counter10_4_b0_0b286615), .carry(counter10_4_carry));
  D_Flip_Flop d_ff_16 (
    .D(counter10_4_b3_6459a22e), .clk(L_6bit_counter_ba3864c1_1_n), .Q(b43));  // open: Qn, preset, reset
  D_Flip_Flop d_ff_17 (
    .D(counter10_4_b2_1cbd16a1), .clk(L_6bit_counter_ba3864c1_1_n), .Q(b42));  // open: Qn, preset, reset
  D_Flip_Flop d_ff_18 (
    .D(counter10_4_b1_bd1f244d), .clk(L_6bit_counter_ba3864c1_1_n), .Q(b41));  // open: Qn, preset, reset
  D_Flip_Flop d_ff_19 (
    .D(counter10_4_b0_0b286615), .clk(L_6bit_counter_ba3864c1_1_n), .Q(b40));  // open: Qn, preset, reset
  L_6bit_counter_ba3864c1 L_6bit_counter_ba3864c1_2 (
    .B2(b52), .B1(b51), .B0(b50), .E2(L_6bit_counter_ba3864c1_2_e2), .E1(L_6bit_counter_ba3864c1_2_e1),
    .E0(L_6bit_counter_ba3864c1_2_e0), .N(L_6bit_counter_ba3864c1_2_n));
  D_Flip_Flop d_ff_20 (.D(L_6bit_counter_ba3864c1_2_e2), .clk(counter10_4_carry), .Q(b52));  // open: Qn, preset, reset
  D_Flip_Flop d_ff_21 (.D(L_6bit_counter_ba3864c1_2_e1), .clk(counter10_4_carry), .Q(b51));  // open: Qn, preset, reset
  D_Flip_Flop d_ff_22 (.D(L_6bit_counter_ba3864c1_2_e0), .clk(counter10_4_carry), .Q(b50));  // open: Qn, preset, reset
  counter10 counter10_5 (
    .b3(b63), .b2(b62), .b1(b61), .b0(b60), .b3_6459a22e(counter10_5_b3_6459a22e),
    .b2_1cbd16a1(counter10_5_b2_1cbd16a1), .b1_bd1f244d(counter10_5_b1_bd1f244d),
    .b0_0b286615(counter10_5_b0_0b286615), .carry(counter10_5_carry));
  D_Flip_Flop d_ff_23 (
    .D(counter10_5_b3_6459a22e), .clk(L_6bit_counter_ba3864c1_2_n), .Q(b63));  // open: Qn, preset, reset
  D_Flip_Flop d_ff_24 (
    .D(counter10_5_b2_1cbd16a1), .clk(L_6bit_counter_ba3864c1_2_n), .Q(b62));  // open: Qn, preset, reset
  D_Flip_Flop d_ff_25 (
    .D(counter10_5_b1_bd1f244d), .clk(L_6bit_counter_ba3864c1_2_n), .Q(b61));  // open: Qn, preset, reset
  D_Flip_Flop d_ff_26 (
    .D(counter10_5_b0_0b286615), .clk(L_6bit_counter_ba3864c1_2_n), .Q(b60));  // open: Qn, preset, reset
  L_2bit_counter_3d0c5adb L_2bit_counter_3d0c5adb_1 (
    .B1(b72), .B0(b71), .E1(L_2bit_counter_3d0c5adb_1_e1), .E0(L_2bit_counter_3d0c5adb_1_e0));  // open: N
  D_Flip_Flop d_ff_27 (.D(L_2bit_counter_3d0c5adb_1_e1), .clk(counter10_5_carry), .Q(b72));  // open: Qn, preset, reset
  D_Flip_Flop d_ff_28 (.D(L_2bit_counter_3d0c5adb_1_e0), .clk(counter10_5_carry), .Q(b71));  // open: Qn, preset, reset
endmodule

module clock24h_display (
  input  clk_10ths,
  output a0,
  output b0,
  output c0,
  output d0,
  output e0,
  output f0,
  output g0,
  output a1,
  output b1,
  output c1,
  output d1,
  output e1,
  output f1,
  output g1,
  output a2,
  output b2,
  output c2,
  output d2,
  output e2,
  output f2,
  output g2,
  output a3,
  output b3,
  output c3,
  output d3,
  output e3,
  output f3,
  output g3,
  output a4,
  output b4,
  output c4,
  output d4,
  output e4,
  output f4,
  output g4,
  output a5,
  output b5,
  output c5,
  output d5,
  output e5,
  output f5,
  output g5,
  output a6,
  output b6,
  output c6,
  output d6,
  output e6,
  output f6,
  output g6,
  output a7,
  output b7,
  output c7,
  output d7,
  output e7,
  output f7,
  output g7
);

  wire clock24h_1_b00, clock24h_1_b01, clock24h_1_b02, clock24h_1_b03, clock24h_1_b10, clock24h_1_b11,
       clock24h_1_b12, clock24h_1_b13, clock24h_1_b20, clock24h_1_b21, clock24h_1_b22, clock24h_1_b23,
       clock24h_1_b30, clock24h_1_b31, clock24h_1_b32, clock24h_1_b40, clock24h_1_b41, clock24h_1_b42,
       clock24h_1_b43, clock24h_1_b50, clock24h_1_b51, clock24h_1_b52, clock24h_1_b60, clock24h_1_b61,
       clock24h_1_b62, clock24h_1_b63, clock24h_1_b71, clock24h_1_b72;

  clock24h clock24h_1 (
    .clock_10thsecond(clk_10ths), .b00(clock24h_1_b00), .b01(clock24h_1_b01), .b02(clock24h_1_b02),
    .b03(clock24h_1_b03), .b10(clock24h_1_b10), .b11(clock24h_1_b11), .b12(clock24h_1_b12),
    .b13(clock24h_1_b13), .b20(clock24h_1_b20), .b21(clock24h_1_b21), .b22(clock24h_1_b22),
    .b23(clock24h_1_b23), .b30(clock24h_1_b30), .b31(clock24h_1_b31), .b32(clock24h_1_b32),
    .b40(clock24h_1_b40), .b41(clock24h_1_b41), .b42(clock24h_1_b42), .b43(clock24h_1_b43),
    .b50(clock24h_1_b50), .b51(clock24h_1_b51), .b52(clock24h_1_b52), .b60(clock24h_1_b60),
    .b61(clock24h_1_b61), .b62(clock24h_1_b62), .b63(clock24h_1_b63), .b71(clock24h_1_b71),
    .b72(clock24h_1_b72));
  bin2display bin2display_8 (
    .b0(clock24h_1_b71), .b1(clock24h_1_b72), .a(a7), .b(b7), .c(c7), .d(d7), .e(e7), .f(f7), .g(g7));  // open: b2, b3
  bin2display bin2display_7 (
    .b0(clock24h_1_b60), .b1(clock24h_1_b61), .b2(clock24h_1_b62), .b3(clock24h_1_b63), .a(a6), .b(b6),
    .c(c6), .d(d6), .e(e6), .f(f6), .g(g6));
  bin2display bin2display_6 (
    .b0(clock24h_1_b50), .b1(clock24h_1_b51), .b2(clock24h_1_b52), .a(a5), .b(b5), .c(c5), .d(d5), .e(e5),
    .f(f5), .g(g5));  // open: b3
  bin2display bin2display_5 (
    .b0(clock24h_1_b40), .b1(clock24h_1_b41), .b2(clock24h_1_b42), .b3(clock24h_1_b43), .a(a4), .b(b4),
    .c(c4), .d(d4), .e(e4), .f(f4), .g(g4));
  bin2display bin2display_4 (
    .b0(clock24h_1_b30), .b1(clock24h_1_b31), .b2(clock24h_1_b32), .a(a3), .b(b3), .c(c3), .d(d3), .e(e3),
    .f(f3), .g(g3));  // open: b3
  bin2display bin2display_3 (
    .b0(clock24h_1_b20), .b1(clock24h_1_b21), .b2(clock24h_1_b22), .b3(clock24h_1_b23), .a(a2), .b(b2),
    .c(c2), .d(d2), .e(e2), .f(f2), .g(g2));
  bin2display bin2display_2 (
    .b0(clock24h_1_b10), .b1(clock24h_1_b11), .b2(clock24h_1_b12), .b3(clock24h_1_b13), .a(a1), .b(b1),
    .c(c1), .d(d1), .e(e1), .f(f1), .g(g1));
  bin2display bin2display_1 (
    .b0(clock24h_1_b00), .b1(clock24h_1_b01), .b2(clock24h_1_b02), .b3(clock24h_1_b03), .a(a0), .b(b0),
    .c(c0), .d(d0), .e(e0), .f(f0), .g(g0));
endmodule
